// Logisim project Proj.circ as structural Verilog: 2 circuits, main circuit main
module main (
  input  in_1
);

  wire _0, _1, _2, _3, _4, _5, _6, _7, _8, _9, CLEAR_out, counter_1_carry, d_ff_1_q, nor_1_out, nor_2_out,
       nor_3_out, nor_4_out, nor_5_out, nor_6_out, not_1_out, not_2_out, not_3_out, not_4_out, not_5_out,
       not_6_out, or_5_out;
  wire [3:0] controlled_buffer_1_out, counter_1_q, demultiplexer_1_out1, demultiplexer_1_out2,
       demultiplexer_1_out3, demultiplexer_1_out4, demultiplexer_1_out5, demultiplexer_1_out6, or_1_out,
       ram_1_data, register_1_q, register_2_q, register_3_q, register_4_q, register_5_q, register_6_q,
       register_7_q, register_8_q;

  Button u__3 (.out(_3));
  Button u__2 (.out(_2));
  Button u__1 (.out(_1));
  Button u__4 (.out(_4));
  Button u__5 (.out(_5));
  Button u__9 (.out(_9));
  Button u__8 (.out(_8));
  Button u__7 (.out(_7));
  Button u__0 (.out(_0));
  Counter #(.width(4), .max('h7), .ongoal("load")) counter_1 (
    .Q(counter_1_q), .carry(counter_1_carry), .clk(or_5_out), .clr(CLEAR_out));  // open: load, D, count
  or or_1 (or_1_out[0], _1, _3, _5, _7, _9);
  or or_2 (or_1_out[1], _2, _3, _6, _7);
  or or_3 (or_1_out[2], _4, _5, _6, _7);
  or or_4 (or_1_out[3], _8, _9);
  Button u__6 (.out(_6));
  D_Flip_Flop d_ff_1 (.clk(counter_1_carry), .D(counter_1_carry), .Q(d_ff_1_q));  // open: Qn, preset, en, reset
  assign controlled_buffer_1_out = not_1_out ? counter_1_q : 4'bz;  // Controlled_Buffer controlled_buffer_1
  not not_1 (not_1_out, d_ff_1_q);
  or or_5 (or_5_out, _0, or_1_out[0], or_1_out[1], or_1_out[2], or_1_out[3]);
  not not_2 (not_2_out, or_5_out);
  Register #(.width(4), .trigger("high")) register_1 (.D(or_1_out), .Q(register_1_q), .clk(or_5_out));  // open: en, clr
  not not_3 (not_3_out, controlled_buffer_1_out[2]);
  not not_4 (not_4_out, controlled_buffer_1_out[1]);
  Register #(.width(4), .trigger("high")) register_2 (
    .D(ram_1_data), .Q(register_2_q), .clk(not_2_out));  // open: en, clr
  RAM #(.addrWidth(4), .dataWidth(4), .bus("separate")) ram_1 (
    .addr(controlled_buffer_1_out), .din(register_1_q), .data(ram_1_data), .clk(not_2_out), .clr(CLEAR_out));  // open: str, sel, ld
  Button CLEAR (.out(CLEAR_out));
  not not_5 (not_5_out, controlled_buffer_1_out[2]);
  Demultiplexer #(.select(4), .width(4), .tristate("true"), .disabled(0), .enable("false")) demultiplexer_1 (
    .out1(demultiplexer_1_out1), .out2(demultiplexer_1_out2), .out3(demultiplexer_1_out3),
    .out4(demultiplexer_1_out4), .out5(demultiplexer_1_out5), .out6(demultiplexer_1_out6), .in(register_2_q),
    .sel(controlled_buffer_1_out));  // open: out0, out7, out8, out9, out10, out11, out12, out13, out14, out15
  nor nor_1 (nor_1_out, controlled_buffer_1_out[0], not_4_out, not_3_out, controlled_buffer_1_out[3]);
  not not_6 (not_6_out, controlled_buffer_1_out[0]);
  nor nor_2 (nor_2_out, controlled_buffer_1_out[0], not_4_out, controlled_buffer_1_out[2], controlled_buffer_1_out[3]);
  nor nor_3 (nor_3_out, not_6_out, not_4_out, controlled_buffer_1_out[2], controlled_buffer_1_out[3]);
  nor nor_4 (nor_4_out, controlled_buffer_1_out[1], not_6_out, controlled_buffer_1_out[2], controlled_buffer_1_out[3]);
  nor nor_5 (nor_5_out, controlled_buffer_1_out[0], controlled_buffer_1_out[1], not_5_out, controlled_buffer_1_out[3]);
  nor nor_6 (nor_6_out, not_6_out, controlled_buffer_1_out[1], not_5_out, controlled_buffer_1_out[3]);
  Hex_Digit_Display hex_digit_display_1 (.value(register_4_q));  // open: dp
  Register #(.width(4), .trigger("high")) register_3 (
    .D(demultiplexer_1_out6), .en(in_1), .Q(register_3_q), .clk(nor_1_out));  // open: clr
  Register #(.width(4), .trigger("high")) register_4 (
    .D(demultiplexer_1_out1), .en(in_1), .Q(register_4_q), .clk(nor_4_out));  // open: clr
  Register #(.width(4), .trigger("high")) register_5 (
    .D(demultiplexer_1_out2), .en(in_1), .Q(register_5_q), .clk(nor_2_out));  // open: clr
  Hex_Digit_Display hex_digit_display_2 (.value(register_6_q));  // open: dp
  Hex_Digit_Display hex_digit_display_3 (.value(register_5_q));  // open: dp
  Hex_Digit_Display hex_digit_display_4 (.value(register_7_q));  // open: dp
  Register #(.width(4), .trigger("high")) register_6 (
    .D(demultiplexer_1_out3), .en(in_1), .Q(register_6_q), .clk(nor_3_out));  // open: clr
  Register #(.width(4), .trigger("high")) register_7 (
    .D(demultiplexer_1_out4), .en(in_1), .Q(register_7_q), .clk(nor_5_out));  // open: clr
  Hex_Digit_Display hex_digit_display_5 (.value(register_8_q));  // open: dp
  Hex_Digit_Display hex_digit_display_6 (.value(register_3_q));  // open: dp
  Register #(.width(4), .trigger("high")) register_8 (
    .D(demultiplexer_1_out5), .en(in_1), .Q(register_8_q), .clk(nor_6_out));  // open: clr
endmodule

module _4bit_Latch (
  input  [3:0] in_1,
  input  in_2,
  input  in_3,
  input  [3:0] in_4,
  output out_5
);

  wire and_1_out, and_2_out, nor_2_out, not_1_out;

  not not_1 (not_1_out, in_3);
  and and_1 (and_1_out, not_1_out, in_2);
  and and_2 (and_2_out, in_3, in_2);
  nor nor_1 (out_5, and_1_out, nor_2_out);
  nor nor_2 (nor_2_out, out_5, and_2_out);
endmodule
